# Fritzing sketch Untitled Sketch (saved by Fritzing 0.8.7b)

parts:
  元件1 = Arduino Uno (Rev3)
  U1 = Thumb Joystick [package=joystick]

nets:
  N1: 元件1.A2, U1.V
  N2: 元件1.A3, U1.H-
  N3: 元件1.GND, U1.H
